// Digital circuit 1X15 SRAM.dig as structural Verilog
module _1X15_SRAM (
  input  [14:0] WD_14_0,
  input  WS,
  input  RS2,
  input  RS1,
  input  Clk,
  output [14:0] RD1_14_0,
  output [14:0] RD2_14_0
);

  _1x1_SRAM _1x1_sram_1 (
    .WD(WD_14_0[0]), .WS(WS), .RS1(RS1), .RS2(RS2), .Clk(Clk), .RD1(RD1_14_0[0]), .RD2(RD2_14_0[0]));
  _1x1_SRAM _1x1_sram_2 (
    .WD(WD_14_0[5]), .WS(WS), .RS1(RS1), .RS2(RS2), .Clk(Clk), .RD1(RD1_14_0[5]), .RD2(RD2_14_0[5]));
  _1x1_SRAM _1x1_sram_3 (
    .WD(WD_14_0[10]), .WS(WS), .RS1(RS1), .RS2(RS2), .Clk(Clk), .RD1(RD1_14_0[10]), .RD2(RD2_14_0[10]));
  _1x1_SRAM _1x1_sram_4 (
    .WD(WD_14_0[1]), .WS(WS), .RS1(RS1), .RS2(RS2), .Clk(Clk), .RD1(RD1_14_0[1]), .RD2(RD2_14_0[1]));
  _1x1_SRAM _1x1_sram_5 (
    .WD(WD_14_0[6]), .WS(WS), .RS1(RS1), .RS2(RS2), .Clk(Clk), .RD1(RD1_14_0[6]), .RD2(RD2_14_0[6]));
  _1x1_SRAM _1x1_sram_6 (
    .WD(WD_14_0[11]), .WS(WS), .RS1(RS1), .RS2(RS2), .Clk(Clk), .RD1(RD1_14_0[11]), .RD2(RD2_14_0[11]));
  _1x1_SRAM _1x1_sram_7 (
    .WD(WD_14_0[2]), .WS(WS), .RS1(RS1), .RS2(RS2), .Clk(Clk), .RD1(RD1_14_0[2]), .RD2(RD2_14_0[2]));
  _1x1_SRAM _1x1_sram_8 (
    .WD(WD_14_0[7]), .WS(WS), .RS1(RS1), .RS2(RS2), .Clk(Clk), .RD1(RD1_14_0[7]), .RD2(RD2_14_0[7]));
  _1x1_SRAM _1x1_sram_9 (
    .WD(WD_14_0[12]), .WS(WS), .RS1(RS1), .RS2(RS2), .Clk(Clk), .RD1(RD1_14_0[12]), .RD2(RD2_14_0[12]));
  _1x1_SRAM _1x1_sram_10 (
    .WD(WD_14_0[3]), .WS(WS), .RS1(RS1), .RS2(RS2), .Clk(Clk), .RD1(RD1_14_0[3]), .RD2(RD2_14_0[3]));
  _1x1_SRAM _1x1_sram_11 (
    .WD(WD_14_0[8]), .WS(WS), .RS1(RS1), .RS2(RS2), .Clk(Clk), .RD1(RD1_14_0[8]), .RD2(RD2_14_0[8]));
  _1x1_SRAM _1x1_sram_12 (
    .WD(WD_14_0[13]), .WS(WS), .RS1(RS1), .RS2(RS2), .Clk(Clk), .RD1(RD1_14_0[13]), .RD2(RD2_14_0[13]));
  _1x1_SRAM _1x1_sram_13 (
    .WD(WD_14_0[4]), .WS(WS), .RS1(RS1), .RS2(RS2), .Clk(Clk), .RD1(RD1_14_0[4]), .RD2(RD2_14_0[4]));
  _1x1_SRAM _1x1_sram_14 (
    .WD(WD_14_0[9]), .WS(WS), .RS1(RS1), .RS2(RS2), .Clk(Clk), .RD1(RD1_14_0[9]), .RD2(RD2_14_0[9]));
  _1x1_SRAM _1x1_sram_15 (
    .WD(WD_14_0[14]), .WS(WS), .RS1(RS1), .RS2(RS2), .Clk(Clk), .RD1(RD1_14_0[14]), .RD2(RD2_14_0[14]));

  // Other names for the same wires on the sheet: RD0 = RD2_14_0[0]; rd0_t = RD1_14_0[0]; RD1 = RD2_14_0[1];
  //   rd1_t = RD1_14_0[1]; RD2 = RD2_14_0[2]; rd2_t = RD1_14_0[2]; RD3 = RD2_14_0[3]; rd3_t = RD1_14_0[3];
  //   RD4 = RD2_14_0[4]; rd4_t = RD1_14_0[4]; RD5 = RD2_14_0[5]; rd5_t = RD1_14_0[5]; RD6 = RD2_14_0[6];
  //   rd6_t = RD1_14_0[6]; RD7 = RD2_14_0[7]; rd7_t = RD1_14_0[7]; RD8 = RD2_14_0[8]; rd8_t = RD1_14_0[8];
  //   RD9 = RD2_14_0[9]; rd9_t = RD1_14_0[9]; RD10 = RD2_14_0[10]; rd10_t = RD1_14_0[10]; RD11 = RD2_14_0[11];
  //   rd11_t = RD1_14_0[11]; RD12 = RD2_14_0[12]; rd12_t = RD1_14_0[12]; RD13 = RD2_14_0[13]; rd13_t = RD1_14_0[13];
  //   RD14 = RD2_14_0[14]; rd14_t = RD1_14_0[14]; WD0 = WD_14_0[0]; WD1 = WD_14_0[1]; WD2 = WD_14_0[2];
  //   WD3 = WD_14_0[3]; WD4 = WD_14_0[4]; WD5 = WD_14_0[5]; WD6 = WD_14_0[6]; WD7 = WD_14_0[7]; WD8 = WD_14_0[8];
  //   WD9 = WD_14_0[9]; WD10 = WD_14_0[10]; WD11 = WD_14_0[11]; WD12 = WD_14_0[12]; WD13 = WD_14_0[13];
  //   WD14 = WD_14_0[14]
endmodule
