// Digital circuit 4 bit program counter set.dig as structural Verilog
module _4_bit_program_counter_set (
  input  [3:0] I_3_0,
  input  Clk,
  output [3:0] O_3_0
);

  _1_bit_register _1_bit_register_1 (.Din(I_3_0[0]), .Sel(1'b1), .Clk(Clk), .Dout(O_3_0[0]));
  _1_bit_register _1_bit_register_2 (.Din(I_3_0[1]), .Sel(1'b1), .Clk(Clk), .Dout(O_3_0[1]));
  _1_bit_register _1_bit_register_3 (.Din(I_3_0[2]), .Sel(1'b1), .Clk(Clk), .Dout(O_3_0[2]));
  _1_bit_register _1_bit_register_4 (.Din(I_3_0[3]), .Sel(1'b1), .Clk(Clk), .Dout(O_3_0[3]));

  // Other names for the same wires on the sheet: D0 = I_3_0[0]; D1 = I_3_0[1]; D2 = I_3_0[2]; D3 = I_3_0[3]
endmodule
