// Digital circuit 6 bit Adder.dig as structural Verilog
module _6_bit_Adder (
  input  [5:0] A_5_0,
  input  [5:0] B_5_0,
  output Cout,
  output [5:0] S_5_0
);

  wire fa_1_p5, fa_2_p4, fa_3_p4, fa_4_p4, fa_5_p4;

  // FA fa_1: pin names not known; wires that end beside it: Cout, A_5_0[5], S_5_0[5], B_5_0[5], fa_1_p5, fa_1_p5
  // FA fa_2: pin names not known; wires that end beside it: A_5_0[4], S_5_0[4], B_5_0[4], fa_2_p4, fa_2_p4
  // FA fa_3: pin names not known; wires that end beside it: A_5_0[3], S_5_0[3], B_5_0[3], fa_3_p4, fa_3_p4
  // FA fa_4: pin names not known; wires that end beside it: A_5_0[2], S_5_0[2], B_5_0[2], fa_4_p4, fa_4_p4
  // FA fa_5: pin names not known; wires that end beside it: A_5_0[1], S_5_0[1], B_5_0[1], fa_5_p4, fa_5_p4
  // FA fa_6: pin names not known; wires that end beside it: A_5_0[0], S_5_0[0], B_5_0[0], 1'b0
endmodule
