// Digital circuit 6 bit ROR.dig as structural Verilog
module _6_bit_ROR (
  input  [5:0] A_5_0,
  input  [5:0] B_5_0,
  output [5:0] S_5_0
);

  Multiplexer #(.Selector_Bits(3)) multiplexer_1 (
    .sel(B_5_0[2:0]), .in_0(A_5_0[5]), .in_1(A_5_0[0]), .in_2(A_5_0[1]), .in_3(A_5_0[2]), .in_4(A_5_0[3]),
    .in_5(A_5_0[4]), .in_6(A_5_0[5]), .in_7(A_5_0[0]), .out(S_5_0[5]));
  Multiplexer #(.Selector_Bits(3)) multiplexer_2 (
    .sel(B_5_0[2:0]), .in_0(A_5_0[4]), .in_1(A_5_0[5]), .in_2(A_5_0[0]), .in_3(A_5_0[1]), .in_4(A_5_0[2]),
    .in_5(A_5_0[3]), .in_6(A_5_0[4]), .in_7(A_5_0[5]), .out(S_5_0[4]));
  Multiplexer #(.Selector_Bits(3)) multiplexer_3 (
    .sel(B_5_0[2:0]), .in_0(A_5_0[3]), .in_1(A_5_0[4]), .in_2(A_5_0[5]), .in_3(A_5_0[0]), .in_4(A_5_0[1]),
    .in_5(A_5_0[2]), .in_6(A_5_0[3]), .in_7(A_5_0[4]), .out(S_5_0[3]));
  Multiplexer #(.Selector_Bits(3)) multiplexer_4 (
    .sel(B_5_0[2:0]), .in_0(A_5_0[2]), .in_1(A_5_0[3]), .in_2(A_5_0[4]), .in_3(A_5_0[5]), .in_4(A_5_0[0]),
    .in_5(A_5_0[1]), .in_6(A_5_0[2]), .in_7(A_5_0[3]), .out(S_5_0[2]));
  Multiplexer #(.Selector_Bits(3)) multiplexer_5 (
    .sel(B_5_0[2:0]), .in_0(A_5_0[1]), .in_1(A_5_0[2]), .in_2(A_5_0[3]), .in_3(A_5_0[4]), .in_4(A_5_0[5]),
    .in_5(A_5_0[0]), .in_6(A_5_0[1]), .in_7(A_5_0[2]), .out(S_5_0[1]));
  Multiplexer #(.Selector_Bits(3)) multiplexer_6 (
    .sel(B_5_0[2:0]), .in_0(A_5_0[0]), .in_1(A_5_0[1]), .in_2(A_5_0[2]), .in_3(A_5_0[3]), .in_4(A_5_0[4]),
    .in_5(A_5_0[5]), .in_6(A_5_0[0]), .in_7(A_5_0[1]), .out(S_5_0[0]));

  // Other names for the same wires on the sheet: A0 = A_5_0[0]; A1 = A_5_0[1]; A2 = A_5_0[2]; A3 = A_5_0[3];
  //   A4 = A_5_0[4]; A5 = A_5_0[5]; Sel0 = B_5_0[0]; Sel1 = B_5_0[1]; Sel2 = B_5_0[2]; S0 = S_5_0[0]; S1 = S_5_0[1];
  //   S2 = S_5_0[2]; S3 = S_5_0[3]; S4 = S_5_0[4]; S5 = S_5_0[5]
endmodule
