// Digital circuit 6 bit X-or.dig as structural Verilog
module _6_bit_X_or (
  input  [5:0] A_5_0,
  input  [5:0] B_5_0,
  output [5:0] S_5_0
);

  xor xor_1 (S_5_0[0], A_5_0[0], B_5_0[0]);
  xor xor_2 (S_5_0[1], A_5_0[1], B_5_0[1]);
  xor xor_3 (S_5_0[2], A_5_0[2], B_5_0[2]);
  xor xor_4 (S_5_0[3], A_5_0[3], B_5_0[3]);
  xor xor_5 (S_5_0[4], A_5_0[4], B_5_0[4]);
  xor xor_6 (S_5_0[5], A_5_0[5], B_5_0[5]);

  // Other names for the same wires on the sheet: A0 = A_5_0[0]; A1 = A_5_0[1]; A2 = A_5_0[2]; A3 = A_5_0[3];
  //   A4 = A_5_0[4]; A5 = A_5_0[5]; B0 = B_5_0[0]; B1 = B_5_0[1]; B2 = B_5_0[2]; B3 = B_5_0[3]; B4 = B_5_0[4];
  //   B5 = B_5_0[5]
endmodule
