// Digital circuit 6-bit ALU.dig as structural Verilog
module _6_bit_ALU (
  input  [5:0] A_5_0,
  input  [5:0] B_5_0,
  input  [1:0] OP_1_0,
  output [5:0] R_5_0,
  output CF,
  output ZF,
  output SF
);

  wire _6_bit_adder_1_cout, nor_1_out, nor_2_out;
  wire [5:0] _6_bit_adder_1_s_5_0, _6_bit_ror_1_s_5_0, _6_bit_x_or_1_s_5_0;

  _6_bit_Adder _6_bit_adder_1 (.B_5_0(B_5_0), .A_5_0(A_5_0), .S_5_0(_6_bit_adder_1_s_5_0), .Cout(_6_bit_adder_1_cout));
  _6_bit_ROR _6_bit_ror_1 (.A_5_0(A_5_0), .B_5_0(B_5_0), .S_5_0(_6_bit_ror_1_s_5_0));
  _6_bit_X_or _6_bit_x_or_1 (.A_5_0(A_5_0), .B_5_0(B_5_0), .S_5_0(_6_bit_x_or_1_s_5_0));
  Multiplexer #(.Selector_Bits(2), .Bits(6)) multiplexer_1 (
    .sel(OP_1_0), .in_0(_6_bit_adder_1_s_5_0), .in_1(_6_bit_ror_1_s_5_0), .in_2(_6_bit_x_or_1_s_5_0),
    .in_3({6{1'b0}}), .out(R_5_0));
  Multiplexer #(.Selector_Bits(2)) multiplexer_2 (
    .sel(OP_1_0), .in_0(_6_bit_adder_1_cout), .in_1(1'b0), .in_2(1'b0), .in_3(1'b0), .out(CF));
  nor nor_1 (nor_1_out, R_5_0[0], R_5_0[1], R_5_0[2]);
  nor nor_2 (nor_2_out, R_5_0[3], R_5_0[4], R_5_0[5]);
  and and_1 (ZF, nor_1_out, nor_2_out);

  assign SF = R_5_0[5];
endmodule
