// Digital circuit 6-bit register set.dig as structural Verilog
module _6_bit_register_set (
  input  [5:0] Din_5_0,
  input  Sel,
  input  Clk,
  output [5:0] Dout_5_0
);

  _1_bit_register _1_bit_register_1 (.Din(Din_5_0[0]), .Sel(Sel), .Clk(Clk), .Dout(Dout_5_0[0]));
  _1_bit_register _1_bit_register_2 (.Din(Din_5_0[1]), .Sel(Sel), .Clk(Clk), .Dout(Dout_5_0[1]));
  _1_bit_register _1_bit_register_3 (.Din(Din_5_0[2]), .Sel(Sel), .Clk(Clk), .Dout(Dout_5_0[2]));
  _1_bit_register _1_bit_register_4 (.Din(Din_5_0[3]), .Sel(Sel), .Clk(Clk), .Dout(Dout_5_0[3]));
  _1_bit_register _1_bit_register_5 (.Din(Din_5_0[4]), .Sel(Sel), .Clk(Clk), .Dout(Dout_5_0[4]));
  _1_bit_register _1_bit_register_6 (.Din(Din_5_0[5]), .Sel(Sel), .Clk(Clk), .Dout(Dout_5_0[5]));

  // Other names for the same wires on the sheet: D0 = Din_5_0[0]; D1 = Din_5_0[1]; D2 = Din_5_0[2]; D3 = Din_5_0[3];
  //   D4 = Din_5_0[4]; D5 = Din_5_0[5]
endmodule
