// Digital circuit 9x15 SRAM.dig as structural Verilog
module _9x15_SRAM (
  input  Clk,
  input  [14:0] WD_14_0,
  input  WE,
  input  [3:0] Wr_3_0,
  input  [3:0] RA2_3_0,
  input  [3:0] RA1_3_0,
  output [14:0] RD1_14_0,
  output [14:0] RD2_14_0
);

  wire D0, D1, D2, D3, D4, D5, D6, D7, D8, R0, R1, R2, R3, R4, R5, R6, R7, R8, RS1_0, RS1_1, RS1_2, RS1_3,
       RS1_4, RS1_5, RS1_6, RS1_7, RS1_8, RS2_0, RS2_1, RS2_2, RS2_3, RS2_4, RS2_5, RS2_6, RS2_7, RS2_8;
  wire [14:0] or_1_out, or_2_out, or_3_out, or_4_out, RD1_0, RD1_1, RD1_2, RD1_3, RD1_4, RD1_5, RD1_6, RD1_7,
       RD1_8, RD2_0, RD2_1, RD2_2, RD2_3, RD2_4, RD2_5, RD2_6, RD2_7, RD2_8;

  Decoder #(.Selector_Bits(4)) decoder_1 (
    .sel(RA1_3_0), .out_0(RS1_0), .out_1(RS1_1), .out_2(RS1_2), .out_3(RS1_3), .out_4(RS1_4), .out_5(RS1_5),
    .out_6(RS1_6), .out_7(RS1_7), .out_8(RS1_8));  // open: out_9, out_10, out_11, out_12, out_13, out_14, out_15
  Decoder #(.Selector_Bits(4)) decoder_2 (
    .sel(RA2_3_0), .out_0(RS2_0), .out_1(RS2_1), .out_2(RS2_2), .out_3(RS2_3), .out_4(RS2_4), .out_5(RS2_5),
    .out_6(RS2_6), .out_7(RS2_7), .out_8(RS2_8));  // open: out_9, out_10, out_11, out_12, out_13, out_14, out_15
  Decoder #(.Selector_Bits(4)) decoder_3 (
    .sel(Wr_3_0), .out_0(R0), .out_1(R1), .out_2(R2), .out_3(R3), .out_4(R4), .out_5(R5), .out_6(R6),
    .out_7(R7), .out_8(R8));  // open: out_9, out_10, out_11, out_12, out_13, out_14, out_15
  and and_1 (D0, R0, WE);
  and and_2 (D2, R2, WE);
  and and_3 (D5, R5, WE);
  and and_4 (D7, R7, WE);
  and and_5 (D4, R4, WE);
  and and_6 (D1, R1, WE);
  and and_7 (D3, R3, WE);
  and and_8 (D6, R6, WE);
  and and_9 (D8, R8, WE);
  _1X15_SRAM _1x15_sram_1 (
    .RS1(RS1_0), .RS2(RS2_0), .WS(D0), .WD_14_0(WD_14_0), .Clk(Clk), .RD1_14_0(RD1_0), .RD2_14_0(RD2_0));
  _1X15_SRAM _1x15_sram_2 (
    .RS1(RS1_1), .RS2(RS2_1), .WS(D1), .WD_14_0(WD_14_0), .Clk(Clk), .RD1_14_0(RD1_1), .RD2_14_0(RD2_1));
  _1X15_SRAM _1x15_sram_3 (
    .RS1(RS1_2), .RS2(RS2_2), .WS(D2), .WD_14_0(WD_14_0), .Clk(Clk), .RD1_14_0(RD1_2), .RD2_14_0(RD2_2));
  _1X15_SRAM _1x15_sram_4 (
    .RS1(RS1_3), .RS2(RS2_3), .WS(D3), .WD_14_0(WD_14_0), .Clk(Clk), .RD1_14_0(RD1_3), .RD2_14_0(RD2_3));
  _1X15_SRAM _1x15_sram_5 (
    .RS1(RS1_4), .RS2(RS2_4), .WS(D4), .WD_14_0(WD_14_0), .Clk(Clk), .RD1_14_0(RD1_4), .RD2_14_0(RD2_4));
  _1X15_SRAM _1x15_sram_6 (
    .RS1(RS1_5), .RS2(RS2_5), .WS(D5), .WD_14_0(WD_14_0), .Clk(Clk), .RD1_14_0(RD1_5), .RD2_14_0(RD2_5));
  _1X15_SRAM _1x15_sram_7 (
    .RS1(RS1_6), .RS2(RS2_6), .WS(D6), .WD_14_0(WD_14_0), .Clk(Clk), .RD1_14_0(RD1_6), .RD2_14_0(RD2_6));
  _1X15_SRAM _1x15_sram_8 (
    .RS1(RS1_7), .RS2(RS2_7), .WS(D7), .WD_14_0(WD_14_0), .Clk(Clk), .RD1_14_0(RD1_7), .RD2_14_0(RD2_7));
  _1X15_SRAM _1x15_sram_9 (
    .RS1(RS1_8), .RS2(RS2_8), .WS(D8), .WD_14_0(WD_14_0), .Clk(Clk), .RD1_14_0(RD1_8), .RD2_14_0(RD2_8));
  assign or_1_out = RD1_0 | RD1_1 | RD1_2 | RD1_3 | RD1_4;  // Or or_1, 15 bits wide
  assign or_2_out = RD1_5 | RD1_6 | RD1_7 | RD1_8;  // Or or_2, 15 bits wide
  assign or_3_out = RD2_0 | RD2_1 | RD2_2 | RD2_3 | RD2_4;  // Or or_3, 15 bits wide
  assign or_4_out = RD2_5 | RD2_6 | RD2_7 | RD2_8;  // Or or_4, 15 bits wide
  assign RD1_14_0 = or_1_out | or_2_out;  // Or or_5, 15 bits wide
  assign RD2_14_0 = or_3_out | or_4_out;  // Or or_6, 15 bits wide

  // Other names for the same wires on the sheet: WD[14:0] = WD_14_0
endmodule
