// Digital circuit CPU.dig as structural Verilog
module CPU (
  input  [14:0] WD_14_0,
  input  [3:0] Wr_3_0,
  input  WE,
  input  Clk,
  input  PC_EN,
  input  [3:0] RA2_3_0,
  output [14:0] RD2_14_0,
  output [5:0] Result_5_0,
  output [2:0] Ra_2_0,
  output [2:0] Rb_2_0,
  output [5:0] Immidiate_Val_5_0,
  output [5:0] A_5_0,
  output [5:0] B_5_0
);

  wire CF, CPU_Clk, IM_Sel, JMP_Sel, Reg_EN, SF, ZF;
  wire [1:0] _9x15_sram_1_rd1_14_0, OPe;
  wire [3:0] _1_1_p1, _1_1_p2, multiplexer_1_out, OP;
  wire [5:0] register_set_1_b_5_0;

  Multiplexer #(.Bits(4)) multiplexer_1 (
    .sel(JMP_Sel), .in_0(_1_1_p1), .in_1({Ra_2_0, Immidiate_Val_5_0[5]}), .out(multiplexer_1_out));
  // _1 _1_1: pin names not known; wires that end beside it: _1_1_p1, _1_1_p2
  _4_bit_program_counter_set _4_bit_program_counter_set_1 (.I_3_0(multiplexer_1_out), .Clk(CPU_Clk), .O_3_0(_1_1_p2));
  and and_1 (CPU_Clk, PC_EN, Clk);
  _9x15_SRAM _9x15_sram_1 (
    .RA1_3_0(_1_1_p2), .RA2_3_0(RA2_3_0), .Wr_3_0(Wr_3_0), .WD_14_0(WD_14_0), .WE(WE), .Clk(Clk),
    .RD1_14_0({OP, Ra_2_0, Immidiate_Val_5_0, _9x15_sram_1_rd1_14_0}), .RD2_14_0(RD2_14_0));
  Register_set register_set_1 (
    .Wr_2_0(Ra_2_0), .Clk(CPU_Clk), .Wrd_5_0(Result_5_0), .WE(1'b1), .A_5_0(A_5_0),
    .B_5_0(register_set_1_b_5_0), .Ra_2_0(Ra_2_0), .Rb_2_0(Immidiate_Val_5_0[5:3]));
  _6_bit_ALU _6_bit_alu_1 (.A_5_0(A_5_0), .B_5_0(B_5_0), .OP_1_0(OPe), .R_5_0(Result_5_0), .CF(CF), .ZF(ZF), .SF(SF));
  Multiplexer #(.Bits(6)) multiplexer_2 (
    .sel(IM_Sel), .in_0(register_set_1_b_5_0), .in_1(Immidiate_Val_5_0), .out(B_5_0));
  Control_Unit control_unit_1 (
    .Op_3_0(OP), .SF(SF), .ZF(ZF), .Op_1_0(OPe), .IM_Sel(IM_Sel), .Reg_EN(Reg_EN), .JMP_Sel(JMP_Sel));

  assign Rb_2_0 = Immidiate_Val_5_0[5:3];

  // Other names for the same wires on the sheet: Val[5:0] = Immidiate_Val_5_0; R2[2:0] = Immidiate_Val_5_0[5:3];
  //   JMP_Add[3:0] = {Ra_2_0, Immidiate_Val_5_0[5]}; R1[2:0] = Ra_2_0; A[5:0] = A_5_0; B[5:0] = B_5_0;
  //   R[5:0] = Result_5_0; RD2[14:0] = RD2_14_0

  // Notes on the sheet:
  //   Register mode(Type of op=00) = 2 bit(type of op) + 2 bit(op) + 3 bit(reg-1) + 3 bit(reg-2) + 5 bit(Don't care)
  //   Immediate mode(Type of op=01) = 2 bit(type of op) + 2 bit(op) + 3 bit(reg-1) + 6 bit(value) + 2 bit(Don't care)
  //   Jump mode(Type of op=10) = 2 bit(type of op) + 2 bit(op) + 4 bit(address) + 7 bit(Don't care)
  //   ALU operation( ADD=00, ROR=01, X-OR=10)
  //   JUMP operation(JMP=00, JG=01)
  //   JG is excuted under the following conditions:
  //   When The Zero Flag(ZF) & the Sign Flag(SF) is Zero(Not set) indicating that the first operand is greater than the second operand.
  //   Instructions:  
  //   	JG START 	->100100010000000
  //   START:	XOR R1, R1 	->000100100100000
  //   JUMPTO:	ADD R1, 5 	->010000100010100
  //   	ROR R1, 2	->011000100001000
  //   OKAY:	ADD R1, 3	->010000100001100
  //   	JMP OKAY	->100001000000000
  //   OUTPUT
endmodule
