// Digital circuit Control Unit.dig as structural Verilog
module Control_Unit (
  input  [3:0] Op_3_0,
  input  SF,
  input  ZF,
  output [1:0] Op_1_0,
  output IM_Sel,
  output Reg_EN,
  output JMP_Sel
);

  wire and_2_out, and_3_out, and_4_out, and_5_out, or_1_out;

  and and_1 (IM_Sel, Op_3_0[2], ~Op_3_0[3]);  // And
  and and_2 (and_2_out, ~Op_3_0[2], ~Op_3_0[3]);  // And
  and and_3 (and_3_out, ~Op_3_0[2], Op_3_0[3]);  // And
  and and_4 (and_4_out, ~Op_3_0[0], ~Op_3_0[1]);  // And
  and and_5 (and_5_out, Op_3_0[0], ~Op_3_0[1], ~SF, ~ZF);  // And
  or or_1 (or_1_out, and_4_out, and_5_out);
  or or_2 (Reg_EN, IM_Sel, and_2_out);
  and and_6 (JMP_Sel, and_3_out, or_1_out);

  assign Op_1_0 = Op_3_0[1:0];
endmodule
