// Digital circuit Register set.dig as structural Verilog
module Register_set (
  input  [2:0] Wr_2_0,
  input  [5:0] Wrd_5_0,
  input  WE,
  input  Clk,
  input  [2:0] Ra_2_0,
  input  [2:0] Rb_2_0,
  output [5:0] A_5_0,
  output [5:0] B_5_0
);

  wire D0, D1, D2, D3, D4, R0, R1, R2, R3, R4;
  wire [5:0] W0, W1, W2, W3, W4;

  and and_1 (D0, R0, WE);
  and and_2 (D2, R2, WE);
  Decoder #(.Selector_Bits(3)) decoder_1 (
    .sel(Wr_2_0), .out_0(R0), .out_1(R1), .out_2(R2), .out_3(R3), .out_4(R4));  // open: out_5, out_6, out_7
  and and_3 (D4, R4, WE);
  and and_4 (D1, R1, WE);
  and and_5 (D3, R3, WE);
  _6_bit_register_set _6_bit_register_set_1 (.Din_5_0(Wrd_5_0), .Sel(D0), .Clk(Clk), .Dout_5_0(W0));
  _6_bit_register_set _6_bit_register_set_2 (.Din_5_0(Wrd_5_0), .Sel(D1), .Clk(Clk), .Dout_5_0(W1));
  _6_bit_register_set _6_bit_register_set_3 (.Din_5_0(Wrd_5_0), .Sel(D2), .Clk(Clk), .Dout_5_0(W2));
  _6_bit_register_set _6_bit_register_set_4 (.Din_5_0(Wrd_5_0), .Sel(D3), .Clk(Clk), .Dout_5_0(W3));
  _6_bit_register_set _6_bit_register_set_5 (.Din_5_0(Wrd_5_0), .Sel(D4), .Clk(Clk), .Dout_5_0(W4));
  Multiplexer #(.Bits(6), .Selector_Bits(3)) multiplexer_1 (
    .sel(Ra_2_0), .in_0(W0), .in_1(W1), .in_2(W2), .in_3(W3), .in_4(W4), .in_5({6{1'b0}}), .in_6({6{1'b0}}),
    .in_7({6{1'b0}}), .out(A_5_0));
  Multiplexer #(.Selector_Bits(3), .Bits(6)) multiplexer_2 (
    .sel(Rb_2_0), .in_0(W0), .in_1(W1), .in_2(W2), .in_3(W3), .in_4(W4), .in_5({6{1'b0}}), .in_6({6{1'b0}}),
    .in_7({6{1'b0}}), .out(B_5_0));

  // Other names for the same wires on the sheet: Ra[2:0] = Ra_2_0; Rb[2:0] = Rb_2_0
endmodule
